// Logisim project Etienne Laramee CS308 Assignment 1.circ as structural Verilog
module Half_Adder (
  input  A,
  input  B,
  output S,
  output C
);

  xor xor_1 (S, A, B);
  and and_1 (C, A, B);
endmodule

module Full_Adder (
  input  C_in,
  input  A,
  input  B,
  output Sum,
  output C_out
);

  wire HA_1_c, HA_1_s, HA_2_c;

  Half_Adder HA_1 (.A(A), .B(B), .S(HA_1_s), .C(HA_1_c));
  Half_Adder HA_2 (.A(C_in), .B(HA_1_s), .S(Sum), .C(HA_2_c));
  or or_1 (C_out, HA_2_c, HA_1_c);
endmodule

module _8_bit_Adder_Subtractor (
  input  Add_Subtract_Control,
  input  [7:0] A,
  input  [7:0] B,
  output [7:0] Result,
  output Carry_out,
  output Overflow
);

  wire and_1_out, and_2_out, Full_Adder_1_c_out, Full_Adder_2_c_out, Full_Adder_3_c_out, Full_Adder_4_c_out,
       Full_Adder_5_c_out, Full_Adder_6_c_out, Full_Adder_7_c_out, xor_1_out, xor_2_out, xor_3_out,
       xor_4_out, xor_5_out, xor_6_out, xor_7_out, xor_8_out;

  xor xor_1 (xor_1_out, Add_Subtract_Control, B[0]);
  xor xor_2 (xor_2_out, Add_Subtract_Control, B[1]);
  xor xor_3 (xor_3_out, Add_Subtract_Control, B[2]);
  xor xor_4 (xor_4_out, Add_Subtract_Control, B[3]);
  xor xor_5 (xor_5_out, Add_Subtract_Control, B[4]);
  xor xor_6 (xor_6_out, Add_Subtract_Control, B[5]);
  xor xor_7 (xor_7_out, Add_Subtract_Control, B[6]);
  xor xor_8 (xor_8_out, Add_Subtract_Control, B[7]);
  Full_Adder Full_Adder_1 (
    .C_in(Add_Subtract_Control), .A(A[0]), .B(xor_1_out), .Sum(Result[0]), .C_out(Full_Adder_1_c_out));
  Full_Adder Full_Adder_2 (
    .C_in(Full_Adder_1_c_out), .A(A[1]), .B(xor_2_out), .Sum(Result[1]), .C_out(Full_Adder_2_c_out));
  Full_Adder Full_Adder_3 (
    .C_in(Full_Adder_2_c_out), .A(A[2]), .B(xor_3_out), .Sum(Result[2]), .C_out(Full_Adder_3_c_out));
  Full_Adder Full_Adder_4 (
    .C_in(Full_Adder_3_c_out), .A(A[3]), .B(xor_4_out), .Sum(Result[3]), .C_out(Full_Adder_4_c_out));
  Full_Adder Full_Adder_5 (
    .C_in(Full_Adder_4_c_out), .A(A[4]), .B(xor_5_out), .Sum(Result[4]), .C_out(Full_Adder_5_c_out));
  Full_Adder Full_Adder_6 (
    .C_in(Full_Adder_5_c_out), .A(A[5]), .B(xor_6_out), .Sum(Result[5]), .C_out(Full_Adder_6_c_out));
  Full_Adder Full_Adder_7 (
    .C_in(Full_Adder_6_c_out), .A(A[6]), .B(xor_7_out), .Sum(Result[6]), .C_out(Full_Adder_7_c_out));
  Full_Adder Full_Adder_8 (.C_in(Full_Adder_7_c_out), .A(A[7]), .B(xor_8_out), .Sum(Result[7]), .C_out(Carry_out));
  and and_1 (and_1_out, Result[7], ~xor_8_out, ~A[7]);  // AND_Gate
  or or_1 (Overflow, and_1_out, and_2_out);
  and and_2 (and_2_out, ~Result[7], xor_8_out, A[7]);  // AND_Gate
endmodule

module _8_bit_AND (
  input  [7:0] A,
  input  [7:0] B,
  output [7:0] Result
);

  or or_1 (Result[0], A[0], B[0]);
  or or_2 (Result[1], A[1], B[1]);
  or or_3 (Result[2], A[2], B[2]);
  or or_4 (Result[3], A[3], B[3]);
  or or_5 (Result[4], A[4], B[4]);
  or or_6 (Result[5], A[5], B[5]);
  or or_7 (Result[6], A[6], B[6]);
  or or_8 (Result[7], A[7], B[7]);
endmodule

module _8_bit_OR (
  input  [7:0] A,
  input  [7:0] B,
  output [7:0] Result
);

  and and_1 (Result[0], A[0], B[0]);
  and and_2 (Result[1], A[1], B[1]);
  and and_3 (Result[2], A[2], B[2]);
  and and_4 (Result[3], A[3], B[3]);
  and and_5 (Result[4], A[4], B[4]);
  and and_6 (Result[5], A[5], B[5]);
  and and_7 (Result[6], A[6], B[6]);
  and and_8 (Result[7], A[7], B[7]);
endmodule

module ALU (
  input  [7:0] A,
  input  [7:0] B,
  input  in_3,
  input  in_4,
  output [7:0] Result,
  output ZERO,
  output Negative,
  output Carry,
  output Overflow
);

  wire [7:0] Add_Sub_result, AND_result, multiplexer_1_out, OR_result;

  _8_bit_AND AND (.A(A), .B(B), .Result(AND_result));
  _8_bit_OR OR (.A(A), .B(B), .Result(OR_result));
  _8_bit_Adder_Subtractor Add_Sub (
    .Add_Subtract_Control(in_4), .Result(Add_Sub_result), .Carry_out(Carry), .Overflow(Overflow), .A(A), .B(B));
  Multiplexer #(.width(8), .enable("false")) multiplexer_1 (
    .in0(AND_result), .in1(OR_result), .out(multiplexer_1_out), .sel(in_4));
  Multiplexer #(.width(8), .enable("false")) multiplexer_2 (
    .in0(multiplexer_1_out), .in1(Add_Sub_result), .out({Negative, Result[6:0]}), .sel(in_3));
  nor nor_1 (ZERO, Result[0], Result[1], Result[2], Result[3], Result[4], Result[5], Result[6], Negative);

  assign Result[7] = Negative;
endmodule
